# Fritzing sketch project fritzing diagram (saved by Fritzing 0.9.6b)
breadboards: 1

parts:
  Part1 = Arduino Nano (Rev3.0) (ICSP)
  Load_Cell1 = Load Cell - Red/white/black/green
  Part2 = HX711 Weighing Sensor Module
  GSM_SIM_GPSR_SMS_SIM900_SIM1 = SIM800L [package=THT]
  2K = Resistor [tolerance=±5% resistance=220 power=0.25 package=THT]
  1k = Resistor [tolerance=±5% resistance=220 power=0.25 package=THT]
  LCD2004-I2C1 = LCD2004-I2C
  VCC1 = Battery block 9V

nets:
  GND: Part1.GND, GSM_SIM_GPSR_SMS_SIM900_SIM1.GND#1, 1k.Pin_1, LCD2004-I2C1.GND
  N1: Part1.D2, 2K.Pin_0
  N2: Part1.D3, GSM_SIM_GPSR_SMS_SIM900_SIM1.SIM_TXD
  N3: Part1.D4, Part2.DO/RX
  N4: Part1.D5, Part2.CK/TX
  N5: Part1.VIN, VCC1.+
  5V: Part1.5V, GSM_SIM_GPSR_SMS_SIM900_SIM1.5V, LCD2004-I2C1.VCC
  N6: Part1.A5, LCD2004-I2C1.SCL
  N7: Part1.A4, LCD2004-I2C1.SDA
  N8: Load_Cell1.wire1, Part2.E+
  N9: Load_Cell1.wire2, Part2.A+
  N10: Load_Cell1.wire3, Part2.E-
  N11: Load_Cell1.wire4, Part2.A-
  N12: GSM_SIM_GPSR_SMS_SIM900_SIM1.SIM_RXD, 2K.Pin_1, 1k.Pin_0

custom parts:
  Load Cell - Red/white/black/green: A rectangle load cell/weighting pressure Sensor with four wires - Red, white, black, green. Normally corresponding with E+, E-, A+, A- respectively.
  LCD2004-I2C: A standard character display with 4x20 characters. Comes in many colors with LCM2004 IIC attached.
